# Fritzing sketch Wheel Board (saved by Fritzing 1.0.2b)
circuit board: 13.9235cm x 7.60908cm

parts:
  UP = Pushbutton [part_number=COM-09190 package="[THT]"]
  DOWN = Pushbutton [part_number=COM-09190 package="[THT]"]
  RIGHT = Pushbutton [part_number=COM-09190 package="[THT]"]
  LEFT = Pushbutton [part_number=COM-09190 package="[THT]"]
  LEFT_MISC_2 = Pushbutton [part_number=COM-09190 package="[THT]"]
  LEFT_MISC_1 = Pushbutton [part_number=COM-09190 package="[THT]"]
  LEFT_MISC_3 = Pushbutton [part_number=COM-09190 package="[THT]"]
  RIGHT_MISC_2 = Pushbutton [part_number=COM-09190 package="[THT]"]
  RIGHT_MISC_1 = Pushbutton [part_number=COM-09190 package="[THT]"]
  RIGHT_MISC_3 = Pushbutton [part_number=COM-09190 package="[THT]"]
  BOXES = Pushbutton [part_number=COM-09190 package="[THT]"]
  LINES = Pushbutton [part_number=COM-09190 package="[THT]"]
  XBOX = Pushbutton [part_number=COM-09190 package="[THT]"]
  PADDLE_LEFT_-_DIGITAL = Pushbutton [part_number=COM-09190 package="[THT]"]
  PADDLE_RIGHT_-_DIGITAL = Pushbutton [part_number=COM-09190 package="[THT]"]
  PADDLE_RIGHT_-_ANALOGUE = Rotary Potentiometer (Small) [maximum_resistance=10kΩ knob_status=50% power=0.5W package=THT]
  PADDLE_LEFT_-_ANALOGUE = Rotary Potentiometer (Small) [maximum_resistance=10kΩ knob_status=50% power=0.5W package=THT]
  J1 = Screw terminal - 2 pins [package=THT]
  J2 = Screw terminal - 2 pins [package=THT]
  J3 = Screw terminal - 2 pins [package=THT]
  J4 = Screw terminal - 2 pins [package=THT]
  Brake = Rotary Potentiometer (Small) [maximum_resistance=10kΩ knob_status=50% power=0.5W package=THT]
  Accelerator = Rotary Potentiometer (Small) [maximum_resistance=10kΩ knob_status=50% power=0.5W package=THT]
  S1 = Round Pushbutton  # not connected
  Steering_Side_DB9 = DB9 Connector [package=db9]
  SparkFun_Pro_Micro1 = SparkFun Pro Micro [part_number=DEV-12640]  # not connected
  Pedal_Side_DB9 = DB9 Connector [package=db9]

nets:
  N1: UP.Pin_1, UP.Pin_2, DOWN.Pin_1, DOWN.Pin_2, RIGHT.Pin_1, RIGHT.Pin_2, LEFT.Pin_1, LEFT.Pin_2, LEFT_MISC_2.Pin_1, LEFT_MISC_2.Pin_2, LEFT_MISC_1.Pin_1, LEFT_MISC_1.Pin_2, LEFT_MISC_3.Pin_1, LEFT_MISC_3.Pin_2, RIGHT_MISC_2.Pin_1, RIGHT_MISC_2.Pin_2, RIGHT_MISC_1.Pin_1, RIGHT_MISC_1.Pin_2, RIGHT_MISC_3.Pin_1, RIGHT_MISC_3.Pin_2, BOXES.Pin_1, BOXES.Pin_2, LINES.Pin_1, LINES.Pin_2, XBOX.Pin_1, XBOX.Pin_2
  N2: UP.Pin_3, UP.Pin_4, DOWN.Pin_3, DOWN.Pin_4, RIGHT.Pin_3, RIGHT.Pin_4, LEFT.Pin_3, LEFT.Pin_4, RIGHT_MISC_2.Pin_3, RIGHT_MISC_2.Pin_4, RIGHT_MISC_1.Pin_3, RIGHT_MISC_1.Pin_4, RIGHT_MISC_3.Pin_3, RIGHT_MISC_3.Pin_4, BOXES.Pin_3, BOXES.Pin_4, LINES.Pin_3, LINES.Pin_4, XBOX.Pin_3, XBOX.Pin_4
  N3: LEFT_MISC_2.Pin_3, LEFT_MISC_2.Pin_4, LEFT_MISC_1.Pin_3, LEFT_MISC_1.Pin_4, LEFT_MISC_3.Pin_3, LEFT_MISC_3.Pin_4
  N4: PADDLE_LEFT_-_DIGITAL.Pin_1, PADDLE_LEFT_-_DIGITAL.Pin_2, J4.pin2
  N5: PADDLE_LEFT_-_DIGITAL.Pin_3, J4.pin1
  N6: PADDLE_RIGHT_-_DIGITAL.Pin_1, PADDLE_RIGHT_-_DIGITAL.Pin_2, J3.pin2
  N7: PADDLE_RIGHT_-_DIGITAL.Pin_3, J3.pin1
  N8: PADDLE_RIGHT_-_ANALOGUE.leg1, J2.pin2
  N9: PADDLE_RIGHT_-_ANALOGUE.wiper, J2.pin1
  N10: PADDLE_LEFT_-_ANALOGUE.leg1, J1.pin2
  N11: PADDLE_LEFT_-_ANALOGUE.wiper, J1.pin1
  N12: Brake.leg1, Steering_Side_DB9.7, Pedal_Side_DB9.7
  N13: Brake.wiper, Steering_Side_DB9.6, Pedal_Side_DB9.6
  N14: Accelerator.leg1, Pedal_Side_DB9.9
  N15: Accelerator.wiper, Steering_Side_DB9.8, Pedal_Side_DB9.8

notes:
  Measure hole diameter and hole position.
  Try to get the foot prints of the buttons to be accurate.
  The pink wire is actually white in the physical object.

custom parts:
  Pushbutton: A generic pushbutton. This is a standard 12mm square momentary button. What we really like is the large button head and good tactile feel (it ‘clicks’ really well). This button is great for user input on a PCB or a good, big reset button on a breadboard. Breadboard friendly! SparkFun Storefront SKU: COM-09190 Modified by: Ho Yun "Bobby" Chan @ SparkFun Electronics Inc.
  SparkFun Pro Micro: This tiny little board does all of the neat-o Arduino tricks that you’re familiar with: 4 channels of 10-bit ADC, 5 PWM pins, 12 DIOs as well as hardware serial connections Rx and Tx. Running at 16MHz and 5V, this board will remind you a lot of your other favorite Arduino-compatible boards but this little guy can go just about anywhere. There is a voltage regulator on board so it can accept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
